# Fritzing sketch Bluetooth (saved by Fritzing 0.9.10b)

parts:
  Part1 = Bluetooth HC-06
  Mod1 = Arduino Sensor Shield v5.0

nets:
  N1: Part1.RXD, Mod1.10-S, Mod1.ParallelLCD-D10
  N2: Part1.TXD, Mod1.11-S, Mod1.ParallelLCD-D11
  N3: Part1.GND, Mod1.9-G, Mod1.ParallelLCD-GND
  N4: Part1.VCC, Mod1.9-V, Mod1.SerialLCD-VCC

custom parts:
  Arduino Sensor Shield v5.0: Arduino Sensor Shield v5.0 provides I2C interface, Bluetooth module communication interface, SD card module communication interface, APC220 wireless RF modules communication interface, RB URF V1.1 ultrasonic sensors interface, 12864 LCD serial and parallel interface, 32 servo controller interfaces. In addition (with the sel jumper removed) allows an external power supply for the servos as the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
