# Fritzing sketch IR Sensor (ky-022) (saved by Fritzing 0.9.10b)

parts:
  Mod1 = Arduino Sensor Shield v5.0
  Mod2 = KY-022 Infrared Receiver Module [package="Breakout board"]

nets:
  N1: Mod1.SD-VCC, Mod1.A0-VCC, Mod2.Vin
  N2: Mod1.SD-GND, Mod1.A0-GND, Mod2.-
  N3: Mod1.URF01-A0, Mod1.A0-SIG, Mod2.S

custom parts:
  Arduino Sensor Shield v5.0: Arduino Sensor Shield v5.0 provides I2C interface, Bluetooth module communication interface, SD card module communication interface, APC220 wireless RF modules communication interface, RB URF V1.1 ultrasonic sensors interface, 12864 LCD serial and parallel interface, 32 servo controller interfaces. In addition (with the sel jumper removed) allows an external power supply for the servos as the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
  KY-022 Infrared Receiver Module: KY-022 IR receiver module, reacts to 38kHz infrared light.
