# Fritzing sketch Line Sensor (saved by Fritzing 0.9.10b)

parts:
  Part1 = KY-033 Tracing Black White Line Hunting Sensor Module For Arduino
  Mod1 = Arduino Sensor Shield v5.0
  Part2 = KY-033 Tracing Black White Line Hunting Sensor Module For Arduino
  Part3 = KY-033 Tracing Black White Line Hunting Sensor Module For Arduino

nets:
  GND: Part1.GND, Mod1.9-G, Mod1.8-G, Mod1.0-G, Mod1.SerialLCD-GND, Part2.GND, Part3.GND
  N1: Part1.V+, Mod1.9-V, Mod1.8-V, Mod1.0-V, Mod1.SerialLCD-VCC, Part2.V+, Part3.V+
  N2: Part1.S, Mod1.COM-RX, Mod1.0-S
  N3: Mod1.9-S, Mod1.ParallelLCD-D9, Part2.S
  N4: Mod1.8-S, Mod1.ParallelLCD-D8, Part3.S

notes:
  Medio
  Extremo izquierdo
  Extremo derecho

custom parts:
  KY-033 Tracing Black White Line Hunting Sensor Module For Arduino: Tracing Black White Line Hunting Sensor Module For Arduino Description: This is KY-033 tracking sensor. The KY-033 measures the intensity of infrared radiation and delivers it as an analog output voltage. Features: Operating voltage: 2.5 - 12V(cannot over12V) working current: 18mA-20mA at 5V Enhanced accuracy Documents: http://www.vishay.com/docs/83760/tcrt5000.pdf
  Arduino Sensor Shield v5.0: Arduino Sensor Shield v5.0 provides I2C interface, Bluetooth module communication interface, SD card module communication interface, APC220 wireless RF modules communication interface, RB URF V1.1 ultrasonic sensors interface, 12864 LCD serial and parallel interface, 32 servo controller interfaces. In addition (with the sel jumper removed) allows an external power supply for the servos as the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
