# Fritzing sketch Motors (saved by Fritzing 0.9.10b)

parts:
  Mod1 = Arduino Sensor Shield v5.0
  S1 = H-Bridge with L298N

nets:
  N1: Mod1.7-S, Mod1.ParallelLCD-D7, S1.IN1
  N2: Mod1.6-S, Mod1.ParallelLCD-D6, S1.ENA
  N3: Mod1.5-S, Mod1.ParallelLCD-D5, S1.IN2
  N4: Mod1.4-S, Mod1.ParallelLCD-D4, S1.IN3
  N5: Mod1.3-S, Mod1.SerialLCD-D3, S1.ENB
  N6: Mod1.2-S, Mod1.ParallelLCD-D2, S1.IN4
  N7: Mod1.2-V, Mod1.SerialLCD-VCC, S1.ENB-5V

custom parts:
  Arduino Sensor Shield v5.0: Arduino Sensor Shield v5.0 provides I2C interface, Bluetooth module communication interface, SD card module communication interface, APC220 wireless RF modules communication interface, RB URF V1.1 ultrasonic sensors interface, 12864 LCD serial and parallel interface, 32 servo controller interfaces. In addition (with the sel jumper removed) allows an external power supply for the servos as the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
  H-Bridge with L298N: h-bridge
