# Fritzing sketch Servo Motor (saved by Fritzing 0.9.10b)

parts:
  Mod1 = Arduino Sensor Shield v5.0
  J1 = Basic Servo

nets:
  N1: Mod1.A5-SIG, J1.pulse
  N2: Mod1.A5-VCC, Mod1.ParallelLCD-VCC, J1.vcc
  N3: Mod1.A5-GND, Mod1.ParallelLCD-GND, J1.gnd

custom parts:
  Arduino Sensor Shield v5.0: Arduino Sensor Shield v5.0 provides I2C interface, Bluetooth module communication interface, SD card module communication interface, APC220 wireless RF modules communication interface, RB URF V1.1 ultrasonic sensors interface, 12864 LCD serial and parallel interface, 32 servo controller interfaces. In addition (with the sel jumper removed) allows an external power supply for the servos as the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
