# Fritzing sketch Ultra Sonic (saved by Fritzing 0.9.10b)

parts:
  Mod1 = Arduino Sensor Shield v5.0
  Part1 = SRF05 Ultrasonic Rangefinder

nets:
  N1: Mod1.13-S, Mod1.ParallelLCD-D13, Part1.Echo
  N2: Mod1.13-V, Mod1.SerialLCD-VCC, Part1.GND
  N3: Mod1.12-S, Mod1.ParallelLCD-D12, Part1.Trig
  N4: Mod1.12-G, Mod1.ParallelLCD-GND, Part1.VCC

custom parts:
  Arduino Sensor Shield v5.0: Arduino Sensor Shield v5.0 provides I2C interface, Bluetooth module communication interface, SD card module communication interface, APC220 wireless RF modules communication interface, RB URF V1.1 ultrasonic sensors interface, 12864 LCD serial and parallel interface, 32 servo controller interfaces. In addition (with the sel jumper removed) allows an external power supply for the servos as the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
